// Logisim project LTD_DÖNEM_PROJESİ.circ as structural Verilog: 1 circuit, main circuit main
module main (
  input  x3,
  input  x2,
  input  x1
);

  wire and_1_out, and_2_out, and_3_out, and_4_out, and_5_out, and_6_out, and_7_out, and_8_out, and_9_out,
       and_10_out, and_11_out, and_12_out, and_13_out, and_14_out, and_15_out, and_16_out, and_17_out,
       and_18_out, and_19_out, and_20_out, and_21_out, and_22_out, and_23_out, and_24_out, and_25_out,
       and_26_out, and_27_out, and_28_out, and_29_out, and_30_out, and_31_out, and_32_out, and_33_out,
       and_34_out, and_35_out, and_36_out, and_37_out, and_38_out, and_39_out, and_40_out, and_41_out,
       and_42_out, and_43_out, and_44_out, and_45_out, and_46_out, and_47_out, and_48_out, and_49_out,
       and_50_out, and_51_out, and_52_out, and_53_out, and_54_out, and_55_out, and_56_out, and_57_out,
       and_58_out, and_59_out, and_60_out, and_61_out, and_62_out, and_63_out, CLK_out, not_1_out, not_2_out,
       not_3_out, not_4_out, not_5_out, not_6_out, not_7_out, not_8_out, not_9_out, not_10_out, not_11_out,
       not_12_out, not_13_out, not_14_out, not_15_out, not_16_out, not_17_out, not_18_out, not_19_out,
       not_20_out, not_21_out, not_22_out, not_23_out, not_24_out, not_25_out, not_26_out, not_27_out,
       not_28_out, not_29_out, not_30_out, not_31_out, not_32_out, not_33_out, not_34_out, not_35_out,
       not_36_out, not_37_out, not_38_out, not_39_out, not_40_out, not_41_out, not_42_out, not_43_out,
       not_44_out, not_45_out, not_46_out, not_47_out, not_48_out, not_49_out, not_50_out, not_51_out,
       not_52_out, not_53_out, not_54_out, not_55_out, not_56_out, not_57_out, not_58_out, not_59_out,
       not_60_out, not_61_out, not_62_out, not_63_out, not_64_out, not_65_out, not_66_out, not_67_out,
       not_68_out, not_69_out, not_70_out, not_71_out, not_72_out, not_73_out, not_74_out, not_75_out,
       not_76_out, not_77_out, not_78_out, not_79_out, not_80_out, not_81_out, not_82_out, not_83_out,
       not_84_out, not_85_out, not_86_out, not_87_out, not_88_out, not_89_out, not_90_out, not_91_out,
       not_92_out, not_93_out, not_94_out, or_1_out, or_2_out, or_3_out, or_4_out, or_5_out, or_6_out,
       or_7_out, or_8_out, or_9_out, or_10_out, or_11_out, or_12_out, Ta_q, Tb_q, Tc_q;

  not not_1 (not_1_out, Ta_q);
  not not_2 (not_2_out, Tc_q);
  not not_3 (not_3_out, x2);
  not not_4 (not_4_out, x1);
  not not_5 (not_5_out, x2);
  not not_6 (not_6_out, x2);
  not not_7 (not_7_out, Tc_q);
  not not_8 (not_8_out, x3);
  not not_9 (not_9_out, Tc_q);
  not not_10 (not_10_out, x2);
  not not_11 (not_11_out, Ta_q);
  not not_12 (not_12_out, Tb_q);
  not not_13 (not_13_out, x1);
  not not_14 (not_14_out, Ta_q);
  not not_15 (not_15_out, Tb_q);
  not not_16 (not_16_out, x1);
  not not_17 (not_17_out, Tb_q);
  not not_18 (not_18_out, Ta_q);
  not not_19 (not_19_out, x2);
  not not_20 (not_20_out, x3);
  and and_1 (and_1_out, not_21_out, not_22_out, x1);
  not not_21 (not_21_out, Tb_q);
  not not_22 (not_22_out, Tc_q);
  and and_2 (and_2_out, not_1_out, not_2_out, x3, not_3_out, not_4_out);
  and and_3 (and_3_out, Tb_q, x3, not_5_out);
  and and_4 (and_4_out, Tb_q, Tc_q, not_6_out);
  and and_5 (and_5_out, Tb_q, Tc_q, x1);
  and and_6 (and_6_out, Tb_q, Tc_q, x3);
  and and_7 (and_7_out, Ta_q, not_7_out, not_8_out);
  and and_8 (and_8_out, Ta_q, not_9_out, not_10_out, x1);
  and and_9 (and_9_out, Ta_q, Tb_q);
  and and_10 (and_10_out, not_11_out, not_12_out, x2, not_13_out);
  and and_11 (and_11_out, not_14_out, not_15_out, Tc_q, not_16_out);
  and and_12 (and_12_out, not_17_out, Tc_q, x2);
  and and_13 (and_13_out, not_18_out, Tc_q, x3);
  and and_14 (and_14_out, Tb_q, not_19_out);
  and and_15 (and_15_out, Tb_q, Tc_q, x1);
  and and_16 (and_16_out, Ta_q, Tc_q, not_20_out);
  and and_17 (and_17_out, Ta_q, Tc_q, x1);
  and and_18 (and_18_out, Ta_q, Tb_q, x1);
  and and_19 (and_19_out, not_24_out, not_23_out, x2);
  not not_23 (not_23_out, Tb_q);
  not not_24 (not_24_out, Ta_q);
  Clock CLK (.out(CLK_out));
  or or_1 (or_1_out, and_2_out, and_3_out, and_4_out, and_5_out, and_6_out, and_7_out, and_8_out, and_9_out);
  or or_2 (or_2_out, and_10_out, and_11_out, and_12_out, and_13_out, and_14_out, and_15_out, and_16_out, and_17_out, and_18_out);
  and and_20 (and_20_out, not_26_out, not_27_out, x3);
  and and_21 (and_21_out, not_25_out, x3);
  not not_25 (not_25_out, Ta_q);
  not not_26 (not_26_out, Tb_q);
  not not_27 (not_27_out, Tc_q);
  T_Flip_Flop Ta (.clk(CLK_out), .T(or_1_out), .Q(Ta_q));  // open: Qn, preset, reset, en
  T_Flip_Flop Tb (.clk(CLK_out), .T(or_2_out), .Q(Tb_q));  // open: Qn, preset, reset, en
  T_Flip_Flop Tc (.clk(CLK_out), .T(or_3_out), .Q(Tc_q));  // open: Qn, preset, reset, en
  or or_3 (or_3_out, and_1_out, and_19_out, and_21_out, and_20_out, and_22_out, and_23_out, and_24_out, and_25_out, and_26_out);
  and and_22 (and_22_out, Tc_q, not_28_out, not_30_out, not_31_out);
  not not_28 (not_28_out, x3);
  and and_23 (and_23_out, not_29_out, Tc_q, x2);
  not not_29 (not_29_out, Tb_q);
  not not_30 (not_30_out, x2);
  not not_31 (not_31_out, x1);
  LED K1 (.in(or_4_out));
  LED S1 (.in(or_6_out));
  LED Y1 (.in(or_11_out));
  and and_24 (and_24_out, Tb_q, not_32_out, x2);
  not not_32 (not_32_out, Tc_q);
  LED K2 (.in(or_10_out));
  LED S2 (.in(or_9_out));
  LED Y2 (.in(or_8_out));
  and and_25 (and_25_out, Tb_q, Tc_q, x1);
  LED K3 (.in(or_12_out));
  LED S3 (.in(or_7_out));
  LED Y3 (.in(or_5_out));
  and and_26 (and_26_out, Ta_q, x1);
  not not_33 (not_33_out, Tb_q);
  not not_34 (not_34_out, Tc_q);
  and and_27 (and_27_out, Ta_q, not_33_out, not_34_out, x3, x2);
  and and_28 (and_28_out, not_37_out, Tb_q);
  and and_29 (and_29_out, not_35_out, not_36_out);
  not not_35 (not_35_out, Tc_q);
  not not_36 (not_36_out, x1);
  not not_37 (not_37_out, Ta_q);
  not not_38 (not_38_out, x1);
  not not_39 (not_39_out, x2);
  or or_4 (or_4_out, and_29_out, and_28_out, and_30_out, and_32_out);
  and and_30 (and_30_out, Ta_q, not_40_out, x3, x2);
  not not_40 (not_40_out, Tb_q);
  not not_41 (not_41_out, Tb_q);
  and and_31 (and_31_out, not_38_out, not_39_out, x3, not_41_out, Ta_q);
  or or_5 (or_5_out, and_27_out, and_31_out, and_33_out, and_35_out);
  and and_32 (and_32_out, Ta_q, Tc_q);
  not not_42 (not_42_out, x2);
  not not_43 (not_43_out, Tc_q);
  and and_33 (and_33_out, not_42_out, x3, not_43_out, Tb_q, not_49_out);
  and and_34 (and_34_out, not_44_out, not_45_out, Tc_q, not_46_out);
  not not_44 (not_44_out, Ta_q);
  not not_45 (not_45_out, Tb_q);
  not not_46 (not_46_out, x1);
  not not_47 (not_47_out, x1);
  not not_48 (not_48_out, x2);
  not not_49 (not_49_out, Ta_q);
  and and_35 (and_35_out, not_47_out, not_48_out, x3, not_52_out, not_53_out);
  or or_6 (or_6_out, and_34_out, and_36_out, and_37_out);
  and and_36 (and_36_out, not_51_out, not_50_out, Tc_q, x2);
  not not_50 (not_50_out, Tb_q);
  not not_51 (not_51_out, Ta_q);
  not not_52 (not_52_out, Tc_q);
  not not_53 (not_53_out, Tb_q);
  and and_37 (and_37_out, not_55_out, not_54_out, Tc_q, x3);
  not not_54 (not_54_out, Tb_q);
  not not_55 (not_55_out, Ta_q);
  and and_38 (and_38_out, x2, Tc_q, Ta_q);
  not not_56 (not_56_out, Tb_q);
  not not_57 (not_57_out, Ta_q);
  not not_58 (not_58_out, x3);
  and and_39 (and_39_out, not_58_out, Tc_q, Ta_q);
  and and_40 (and_40_out, x1, Tc_q, Ta_q);
  or or_7 (or_7_out, and_38_out, and_40_out, and_39_out);
  and and_41 (and_41_out, not_57_out, not_56_out, not_60_out, x1);
  not not_59 (not_59_out, Ta_q);
  not not_60 (not_60_out, Tc_q);
  and and_42 (and_42_out, Tb_q, Ta_q);
  and and_43 (and_43_out, not_59_out, not_61_out, not_63_out, not_62_out, x1);
  not not_61 (not_61_out, Tb_q);
  not not_62 (not_62_out, x2);
  not not_63 (not_63_out, x3);
  not not_64 (not_64_out, Ta_q);
  and and_44 (and_44_out, Tc_q, not_64_out);
  or or_8 (or_8_out, and_50_out, and_51_out, and_52_out, and_53_out, and_54_out);
  or or_9 (or_9_out, and_55_out, and_56_out, and_57_out);
  or or_10 (or_10_out, and_58_out, and_59_out, and_60_out, and_61_out, and_62_out);
  or or_11 (or_11_out, and_41_out, and_43_out, and_45_out, and_48_out, and_63_out);
  and and_45 (and_45_out, not_65_out, not_67_out, not_66_out, x1);
  not not_65 (not_65_out, Tb_q);
  not not_66 (not_66_out, x3);
  not not_67 (not_67_out, Tc_q);
  not not_68 (not_68_out, x2);
  not not_69 (not_69_out, Ta_q);
  and and_46 (and_46_out, x1, not_68_out, not_76_out, not_74_out);
  and and_47 (and_47_out, x2, not_69_out);
  or or_12 (or_12_out, and_42_out, and_44_out, and_47_out, and_46_out, and_49_out);
  and and_48 (and_48_out, not_72_out, not_70_out, not_71_out, x1);
  not not_70 (not_70_out, Tc_q);
  not not_71 (not_71_out, x2);
  not not_72 (not_72_out, Tb_q);
  not not_73 (not_73_out, Tc_q);
  not not_74 (not_74_out, Tb_q);
  not not_75 (not_75_out, x3);
  not not_76 (not_76_out, Tc_q);
  and and_49 (and_49_out, not_75_out, not_73_out);
  and and_50 (and_50_out, not_77_out, x2, not_78_out, Tb_q);
  and and_51 (and_51_out, not_79_out, x2, not_80_out, Tb_q);
  and and_52 (and_52_out, x2, not_81_out, Tb_q, not_82_out);
  and and_53 (and_53_out, x2, x3, not_83_out, not_84_out);
  and and_54 (and_54_out, not_85_out, x2, not_86_out, not_87_out);
  and and_55 (and_55_out, x3, Tc_q, Tb_q);
  and and_56 (and_56_out, x1, Tc_q, Tb_q);
  and and_57 (and_57_out, not_88_out, Tc_q, Tb_q);
  and and_58 (and_58_out, x1, Ta_q);
  and and_59 (and_59_out, not_89_out, Ta_q);
  and and_60 (and_60_out, Tc_q, not_90_out);
  and and_61 (and_61_out, x1, not_91_out, not_92_out);
  and and_62 (and_62_out, not_93_out, not_94_out);
  and and_63 (and_63_out, Ta_q, Tb_q, x1);
  not not_77 (not_77_out, x1);
  not not_78 (not_78_out, x3);
  not not_79 (not_79_out, x1);
  not not_80 (not_80_out, Tc_q);
  not not_81 (not_81_out, Tc_q);
  not not_82 (not_82_out, Ta_q);
  not not_83 (not_83_out, Tc_q);
  not not_84 (not_84_out, Ta_q);
  not not_85 (not_85_out, x1);
  not not_86 (not_86_out, Tc_q);
  not not_87 (not_87_out, Ta_q);
  not not_88 (not_88_out, x2);
  not not_89 (not_89_out, Tb_q);
  not not_90 (not_90_out, Tb_q);
  not not_91 (not_91_out, x3);
  not not_92 (not_92_out, Tb_q);
  not not_93 (not_93_out, x2);
  not not_94 (not_94_out, Tc_q);

  // Notes on the sheet:
  //   Yol 1
  //   Yol 2
  //   Yol 3
  //   yandığı anda Yol 1'de Yeşik ışık yanıyor. Sürekli bu döngüde kalıyorlar. 
  //   yandığı anda Yol 1'de Yeşik ışık yanıyor. Sürekli bu döngüde kalıyorlar. 
  //   yandığı anda Yol 1'de Yeşik ışık yanıyor. Sürekli bu döngüde kalıyorlar. 
  //   Yol 1'de Yeşik ışık yanıyor. Sürekli bu döngüde kalıyorlar.
  //   - Tüm Yollar boş olup, trafik olmadığında, tüm ışıklarda sürekli Kırmızı ışık yanıyor. 
  //   - Yol 1'de trafik olduğunda sensör(x1) aktif hale gelip Yol 1'de sürekli Yeşil ışık yanıyor. 
  //   - Yol 2'de trafik olduğunda sensör(x2) aktif hale gelip Yol 2'de sürekli Yeşil ışık yanıyor. 
  //   - Yol 3'de trafik olduğunda sensör(x3) aktif hale gelip Yol 3'de sürekli Yeşil ışık yanıyor. 
  //   - Yol 1 ve Yol 2'de trafik olduğunda sensörler(x1 ve x2) aktif hale gelip sırasıyla teker teker
  //   - Yol 1 ve Yol 3'de trafik olduğunda sensörler(x1 ve x3) aktif hale gelip sırasıyla teker teker 
  //   - Yol 2 ve Yol 3'de trafik olduğunda sensörler(x2 ve x3) aktif hale gelip sırasıyla teker teker 
  //   - Tüm Yollarda trafik olduğunda sensörler(x1, x2 ve x3) aktif hale gelip sırasıyla teker teker 
  //   Yol 1 ve Yol 2'de Yeşil ışık yanıyor. Yol 1'de Yeşil ışık yandıktan sonra Sarı ışık yanıyor ve ondan sonra 
  //   Kırmızı ışık yandığı anda Yol 2'de Yeşil ışık yanıyor. Sonra Sarı ışık yanıp ondan sonra Kırmızı ışık 
  //   Yol 1 ve Yol 3'de Yeşil ışık yanıyor. Yol 1'de Yeşil ışık yandıktan sonra Sarı ışık yanıyor ve ondan sonra 
  //   Kırmızı ışık yandığı anda Yol 3'de Yeşil ışık yanıyor. Sonra Sarı ışık yanıp ondan sonra Kırmızı ışık 
  //   Yol 2 ve Yol 3'de Yeşil ışık yanıyor. Yol 2'de Yeşil ışık yandıktan sonra Sarı ışık yanıyor ve ondan sonra 
  //   Kırmızı ışık yandığı anda Yol 3'de Yeşil ışık yanıyor. Sonra Sarı ışık yanıp ondan sonra Kırmızı ışık 
  //   Yol 1, Yol 2 ve Yol 3'de Yeşil ışık yanıyor. Yol 1'de Yeşil ışık yandıktan sonra Sarı ışık yanıyor ve ondan sonra 
  //   Kırmızı ışık yandığı anda Yol 2'de Yeşil ışık yanıyor. Sonra Sarı ışık yanıp ondan sonra Kırmızı ışık 
  //   yandığı anda Yol 3'de Yeşik ışık yanıyor ve sonra Sarı ışık yanıp ondan sonra Kırmızı ışık yandığı anda 
endmodule
